// Logisim project CRC.circ as structural Verilog: 2 circuits, main circuit CRC
module CRC (
  input  [7:0] A,
  input  [3:0] B,
  output [10:0] out_3
);

  wire [2:0] n4_bit_div_1_remainder, n4_bit_div_2_remainder, n4_bit_div_3_remainder, n4_bit_div_4_remainder,
       n4_bit_div_5_remainder, n4_bit_div_6_remainder, n4_bit_div_7_remainder;

  // Probe on {A, 3'b000}
  _4_bit_div u_4_bit_div_1 (.A(A[7:4]), .B(B), .remainder(n4_bit_div_1_remainder));  // open: D商
  _4_bit_div u_4_bit_div_2 (.A({n4_bit_div_1_remainder, A[3]}), .B(B), .remainder(n4_bit_div_2_remainder));  // open: D商
  _4_bit_div u_4_bit_div_3 (.A({n4_bit_div_2_remainder, A[2]}), .B(B), .remainder(n4_bit_div_3_remainder));  // open: D商
  _4_bit_div u_4_bit_div_4 (.A({n4_bit_div_3_remainder, A[1]}), .B(B), .remainder(n4_bit_div_4_remainder));  // open: D商
  _4_bit_div u_4_bit_div_5 (.A({n4_bit_div_4_remainder, A[0]}), .B(B), .remainder(n4_bit_div_5_remainder));  // open: D商
  _4_bit_div u_4_bit_div_6 (.A({n4_bit_div_5_remainder, 1'b0}), .B(B), .remainder(n4_bit_div_6_remainder));  // open: D商
  _4_bit_div u_4_bit_div_7 (.A({n4_bit_div_6_remainder, 1'b0}), .B(B), .remainder(n4_bit_div_7_remainder));  // open: D商
  _4_bit_div u_4_bit_div_8 (.A({n4_bit_div_7_remainder, 1'b0}), .B(B), .remainder(out_3[2:0]));  // open: D商

  assign out_3[10:3] = A;

  // Other names for the same wires on the sheet: divisor[3:0] = B; input[7:0] = A
endmodule

module _4_bit_div (
  input  [3:0] A,
  input  [3:0] B,
  output \D商 ,
  output [2:0] remainder
);

  wire [3:0] multiplexer_1_out, xor_1_out;

  BitSelector #(.width(4)) bitselector_1 (.in(A), .out(\D商 ), .sel(2'b11));
  assign xor_1_out = A ^ B;  // XOR_Gate xor_1, 4 bits wide
  // Probe on multiplexer_1_out
  Multiplexer #(.width(4), .disabled(0)) multiplexer_1 (
    .in0(A), .in1(xor_1_out), .out(multiplexer_1_out), .sel(\D商 ));  // open: en
  Bit_Extender #(.in_width(4), .out_width(3)) bit_extender_1 (.in(multiplexer_1_out), .out(remainder));
endmodule
