// Logisim project fsm.circ as structural Verilog: 3 circuits, main circuit fsm
module fsm (
  input  [1:0] In,
  input  CLR,
  output Z
);

  wire clock_1_out, multiplexer_1_out, multiplexer_2_out, register_1_q, register_2_q, transfer_state_1_ss0,
       transfer_state_1_ss1;

  transfer_state transfer_state_1 (
    .S1(register_1_q), .S0(register_2_q), .in1(In[1]), .in0(In[0]), .SS1(transfer_state_1_ss1),
    .SS0(transfer_state_1_ss0));
  Multiplexer multiplexer_1 (.in0(transfer_state_1_ss1), .in1(1'b0), .out(multiplexer_1_out), .sel(CLR));  // open: en
  Multiplexer multiplexer_2 (.in0(transfer_state_1_ss0), .in1(1'b0), .out(multiplexer_2_out), .sel(CLR));  // open: en
  Clock clock_1 (.out(clock_1_out));
  Register #(.width(1)) register_1 (.D(multiplexer_1_out), .Q(register_1_q), .clk(clock_1_out));  // open: en, clr
  Register #(.width(1)) register_2 (.D(multiplexer_2_out), .Q(register_2_q), .clk(clock_1_out));  // open: en, clr
  \output  output_1 (.S1(register_1_q), .S0(register_2_q), .in1(In[1]), .in0(In[0]), .Z(Z));
endmodule

module transfer_state (
  input  S1,
  input  S0,
  input  in1,
  input  in0,
  output SS1,
  output SS0
);

  wire and_1_out, and_2_out, and_3_out, and_4_out, and_5_out, and_6_out, and_7_out, and_8_out, and_9_out,
       and_10_out, and_11_out, and_12_out, and_13_out, not_1_out, not_2_out, not_3_out, not_4_out, not_5_out,
       not_6_out, not_7_out, not_8_out, not_9_out, not_10_out, not_11_out, not_12_out, not_13_out, or_1_out,
       or_2_out;

  not not_1 (not_1_out, S1);
  and and_1 (and_1_out, not_1_out, S0);
  not not_2 (not_2_out, in1);
  not not_3 (not_3_out, S1);
  and and_2 (and_2_out, not_3_out, S0);
  not not_4 (not_4_out, in0);
  not not_5 (not_5_out, S0);
  not not_6 (not_6_out, S1);
  and and_3 (and_3_out, not_6_out, not_7_out);
  not not_7 (not_7_out, S0);
  not not_8 (not_8_out, in1);
  and and_4 (and_4_out, not_8_out, in0);
  not not_9 (not_9_out, S1);
  and and_5 (and_5_out, not_9_out, S0);
  not not_10 (not_10_out, in0);
  not not_11 (not_11_out, S0);
  and and_6 (and_6_out, and_1_out, not_2_out);
  and and_7 (and_7_out, and_2_out, not_4_out);
  and and_8 (and_8_out, S1, not_5_out);
  not not_12 (not_12_out, in0);
  and and_9 (and_9_out, and_3_out, and_4_out);
  and and_10 (and_10_out, and_5_out, not_10_out);
  and and_11 (and_11_out, S1, not_11_out);
  not not_13 (not_13_out, in0);
  or or_1 (or_1_out, and_6_out, and_7_out);
  and and_12 (and_12_out, and_8_out, not_12_out);
  or or_2 (or_2_out, and_9_out, and_10_out);
  and and_13 (and_13_out, and_11_out, not_13_out);
  or or_3 (SS1, or_1_out, and_12_out);
  or or_4 (SS0, or_2_out, and_13_out);
endmodule

module \output  (
  input  S1,
  input  S0,
  input  in1,
  input  in0,
  output Z
);

  wire and_1_out, not_1_out;

  and and_1 (and_1_out, S1, S0);
  not not_1 (not_1_out, in0);
  and and_2 (Z, and_1_out, not_1_out);
endmodule
