// Logisim project ftoi.circ as structural Verilog: 3 circuits, main circuit ftoi
module ftoi (
  input  [15:0] float,
  output [31:0] \int 
);

  wire judge_1_o;
  wire [15:0] demultiplexer_1_out1;
  wire [31:0] ari_1_out_2;

  Demultiplexer #(.width(16), .disabled(0), .enable("false")) demultiplexer_1 (
    .out1(demultiplexer_1_out1), .in(float), .sel(judge_1_o));  // open: out0
  judge judge_1 (.exponent(float[14:10]), .O(judge_1_o));
  Ari ari_1 (.in_1(demultiplexer_1_out1), .out_2(ari_1_out_2));
  Multiplexer #(.width(32), .disabled(0), .enable("false")) multiplexer_1 (
    .in0({32{1'b0}}), .in1(ari_1_out_2), .out(\int ), .sel(judge_1_o));
endmodule

module judge (
  input  [4:0] exponent,
  output O
);

  wire comparator_1_eq, comparator_1_gt, comparator_2_eq, not_1_out, or_1_out;

  Comparator #(.width(5), .mode("unsigned")) comparator_1 (
    .a(exponent), .b(5'b01111), .gt(comparator_1_gt), .eq(comparator_1_eq));  // open: lt
  Comparator #(.width(5), .mode("unsigned")) comparator_2 (
    .a(exponent), .b({5{1'b1}}), .eq(comparator_2_eq));  // open: gt, lt
  or or_1 (or_1_out, comparator_1_gt, comparator_1_eq);
  not not_1 (not_1_out, comparator_2_eq);
  and and_1 (O, or_1_out, not_1_out);
endmodule

module Ari (
  input  [15:0] in_1,
  output [31:0] out_2
);

  wire [3:0] bit_extender_1_out;
  wire [4:0] subtractor_1_out;
  wire [15:0] shifter_1_out;
  wire [31:0] bit_extender_2_out, negator_1_out;

  // Probe on 5'b11110
  Subtractor #(.width(5)) subtractor_1 (.a(5'b11110), .b(in_1[14:10]), .out(subtractor_1_out));  // open: bin, bout
  // Probe on {1'b1, in_1[9:0], {5{1'b0}}}
  // Probe on subtractor_1_out
  Bit_Extender #(.in_width(5), .out_width(4)) bit_extender_1 (.in(subtractor_1_out), .out(bit_extender_1_out));
  Shifter #(.width(16), .shift("lr")) shifter_1 (
    .in({1'b1, in_1[9:0], {5{1'b0}}}), .\dist (bit_extender_1_out), .out(shifter_1_out));
  // Probe on bit_extender_1_out
  assign bit_extender_2_out = {{16{1'b0}}, shifter_1_out};  // Bit_Extender bit_extender_2
  Negator #(.width(32)) negator_1 (.in(bit_extender_2_out), .out(negator_1_out));
  Multiplexer #(.width(32), .disabled(0), .enable("false")) multiplexer_1 (
    .in0(bit_extender_2_out), .in1(negator_1_out), .out(out_2), .sel(in_1[15]));
endmodule
