// Logisim project grf.circ as structural Verilog: 2 circuits, main circuit grf
module grf (
  input  WE,
  input  clk,
  input  [4:0] A1,
  input  [4:0] A2,
  input  [4:0] A3,
  input  [31:0] WD,
  input  reset,
  output [31:0] RD1,
  output [31:0] RD2
);

  wire [31:0] _00, _000, _001, _01, _002, _02, _003, _03, _004, _04, _005, _05, _006, _06, _007, _07, _008,
       _08, _009, _09, _010, _10, _011, _11, _012, _12, _013, _13, _014, _14, _015, _15, _016, _16, _017,
       _17, _018, _18, _019, _19, _020, _20, _021, _21, _022, _22, _023, _23, _024, _24, _025, _25, _026,
       _26, _027, _27, _028, _28, _029, _29, _030, _30, _031, _31, and_1_out, and_2_out;

  Register #(.width(32)) u__00 (.D(_000), .en(WE), .Q(_00), .clk(clk), .clr(reset));
  Register #(.width(32)) u__01 (.D(_001), .en(WE), .Q(_01), .clk(clk), .clr(reset));
  Register #(.width(32)) u__02 (.D(_002), .en(WE), .Q(_02), .clk(clk), .clr(reset));
  Register #(.width(32)) u__03 (.D(_003), .en(WE), .Q(_03), .clk(clk), .clr(reset));
  Register #(.width(32)) u__04 (.D(_004), .en(WE), .Q(_04), .clk(clk), .clr(reset));
  Register #(.width(32)) u__05 (.D(_005), .en(WE), .Q(_05), .clk(clk), .clr(reset));
  Register #(.width(32)) u__06 (.D(_006), .en(WE), .Q(_06), .clk(clk), .clr(reset));
  Register #(.width(32)) u__07 (.D(_007), .en(WE), .Q(_07), .clk(clk), .clr(reset));
  Demultiplexer #(.select(5), .width(32), .tristate("true"), .disabled(0), .enable("false")) demultiplexer_1 (
    .out0(_000), .out1(_001), .out2(_002), .out3(_003), .out4(_004), .out5(_005), .out6(_006), .out7(_007),
    .out8(_008), .out9(_009), .out10(_010), .out11(_011), .out12(_012), .out13(_013), .out14(_014),
    .out15(_015), .out16(_016), .out17(_017), .out18(_018), .out19(_019), .out20(_020), .out21(_021),
    .out22(_022), .out23(_023), .out24(_024), .out25(_025), .out26(_026), .out27(_027), .out28(_028),
    .out29(_029), .out30(_030), .out31(_031), .in(WD), .sel(A3));
  Register #(.width(32)) u__08 (.D(_008), .en(WE), .Q(_08), .clk(clk), .clr(reset));
  Register #(.width(32)) u__09 (.D(_009), .en(WE), .Q(_09), .clk(clk), .clr(reset));
  Register #(.width(32)) u__10 (.D(_010), .en(WE), .Q(_10), .clk(clk), .clr(reset));
  Register #(.width(32)) u__11 (.D(_011), .en(WE), .Q(_11), .clk(clk), .clr(reset));
  Register #(.width(32)) u__12 (.D(_012), .en(WE), .Q(_12), .clk(clk), .clr(reset));
  Register #(.width(32)) u__13 (.D(_013), .en(WE), .Q(_13), .clk(clk), .clr(reset));
  Register #(.width(32)) u__14 (.D(_014), .en(WE), .Q(_14), .clk(clk), .clr(reset));
  Register #(.width(32)) u__15 (.D(_015), .en(WE), .Q(_15), .clk(clk), .clr(reset));
  Register #(.width(32)) u__16 (.D(_016), .en(WE), .Q(_16), .clk(clk), .clr(reset));
  Register #(.width(32)) u__17 (.D(_017), .en(WE), .Q(_17), .clk(clk), .clr(reset));
  Register #(.width(32)) u__18 (.D(_018), .en(WE), .Q(_18), .clk(clk), .clr(reset));
  Register #(.width(32)) u__19 (.D(_019), .en(WE), .Q(_19), .clk(clk), .clr(reset));
  Register #(.width(32)) u__20 (.D(_020), .en(WE), .Q(_20), .clk(clk), .clr(reset));
  Register #(.width(32)) u__21 (.D(_021), .en(WE), .Q(_21), .clk(clk), .clr(reset));
  Register #(.width(32)) u__22 (.D(_022), .en(WE), .Q(_22), .clk(clk), .clr(reset));
  Register #(.width(32)) u__23 (.D(_023), .en(WE), .Q(_23), .clk(clk), .clr(reset));
  Register #(.width(32)) u__24 (.D(_024), .en(WE), .Q(_24), .clk(clk), .clr(reset));
  Register #(.width(32)) u__25 (.D(_025), .en(WE), .Q(_25), .clk(clk), .clr(reset));
  Register #(.width(32)) u__26 (.D(_026), .en(WE), .Q(_26), .clk(clk), .clr(reset));
  Register #(.width(32)) u__27 (.D(_027), .en(WE), .Q(_27), .clk(clk), .clr(reset));
  Register #(.width(32)) u__28 (.D(_028), .en(WE), .Q(_28), .clk(clk), .clr(reset));
  Register #(.width(32)) u__29 (.D(_029), .en(WE), .Q(_29), .clk(clk), .clr(reset));
  Register #(.width(32)) u__30 (.D(_030), .en(WE), .Q(_30), .clk(clk), .clr(reset));
  Register #(.width(32)) u__31 (.D(_031), .en(WE), .Q(_31), .clk(clk), .clr(reset));
  assign and_1_out = {32{1'b0}} & _00;  // AND_Gate and_1, 32 bits wide
  Multiplexer #(.select(5), .width(32), .disabled(0), .enable("false")) multiplexer_1 (
    .in0(and_1_out), .in1(_01), .in2(_02), .in3(_03), .in4(_04), .in5(_05), .in6(_06), .in7(_07), .in8(_08),
    .in9(_09), .in10(_10), .in11(_11), .in12(_12), .in13(_13), .in14(_14), .in15(_15), .in16(_16),
    .in17(_17), .in18(_18), .in19(_19), .in20(_20), .in21(_21), .in22(_22), .in23(_23), .in24(_24),
    .in25(_25), .in26(_26), .in27(_27), .in28(_28), .in29(_29), .in30(_30), .in31(_31), .out(RD1), .sel(A1));
  assign and_2_out = {32{1'b0}} & _00;  // AND_Gate and_2, 32 bits wide
  Multiplexer #(.select(5), .width(32), .disabled(0), .enable("false")) multiplexer_2 (
    .in0(and_2_out), .in1(_01), .in2(_02), .in3(_03), .in4(_04), .in5(_05), .in6(_06), .in7(_07), .in8(_08),
    .in9(_09), .in10(_10), .in11(_11), .in12(_12), .in13(_13), .in14(_14), .in15(_15), .in16(_16),
    .in17(_17), .in18(_18), .in19(_19), .in20(_20), .in21(_21), .in22(_22), .in23(_23), .in24(_24),
    .in25(_25), .in26(_26), .in27(_27), .in28(_28), .in29(_29), .in30(_30), .in31(_31), .out(RD2), .sel(A2));
endmodule

module control_output (
  input  [31:0] in_1,
  input  [31:0] in_2,
  input  [31:0] in_3,
  input  [31:0] in_4,
  input  [31:0] in_5,
  input  [31:0] in_6,
  input  [31:0] in_7,
  input  [31:0] in_8,
  input  [31:0] in_9,
  input  [31:0] in_10,
  input  [31:0] in_11,
  input  [31:0] in_12,
  input  [31:0] in_13,
  input  [31:0] in_14,
  input  [31:0] in_15,
  input  [31:0] in_16,
  input  [31:0] in_17,
  input  [31:0] in_18,
  input  [31:0] in_19,
  input  [31:0] in_20,
  input  [31:0] in_21,
  input  [31:0] in_22,
  input  [31:0] in_23,
  input  [31:0] in_24,
  input  [31:0] in_25,
  input  [31:0] in_26,
  input  [31:0] in_27,
  input  [31:0] in_28,
  input  [31:0] in_29,
  input  [31:0] in_30,
  input  [31:0] in_31,
  input  [31:0] in_32,
  input  [4:0] in_33,
  output [31:0] out_34
);

  Multiplexer #(.select(5), .width(32), .disabled(0)) multiplexer_1 (
    .in0(in_1), .in1(in_5), .in2(in_9), .in3(in_13), .in4(in_17), .in5(in_21), .in6(in_25), .in7(in_29),
    .in8(in_2), .in9(in_6), .in10(in_10), .in11(in_14), .in12(in_18), .in13(in_22), .in14(in_26),
    .in15(in_30), .in16(in_3), .in17(in_7), .in18(in_11), .in19(in_15), .in20(in_19), .in21(in_23),
    .in22(in_27), .in23(in_31), .in24(in_4), .in25(in_8), .in26(in_12), .in27(in_16), .in28(in_20),
    .in29(in_24), .in30(in_28), .in31(in_32), .out(out_34), .sel(in_33));  // open: en

  // Other names for the same wires on the sheet: _00[31:0] = in_1; _01[31:0] = in_5; _02[31:0] = in_9;
  //   _03[31:0] = in_13; _04[31:0] = in_17; _05[31:0] = in_21; _06[31:0] = in_25; _07[31:0] = in_29; _08[31:0] = in_2;
  //   _09[31:0] = in_6; _10[31:0] = in_10; _11[31:0] = in_14; _12[31:0] = in_18; _13[31:0] = in_22; _14[31:0] = in_26;
  //   _15[31:0] = in_30; _16[31:0] = in_3; _17[31:0] = in_7; _18[31:0] = in_11; _19[31:0] = in_15; _20[31:0] = in_19;
  //   _21[31:0] = in_23; _22[31:0] = in_27; _23[31:0] = in_31; _24[31:0] = in_4; _25[31:0] = in_8; _26[31:0] = in_12;
  //   _27[31:0] = in_16; _28[31:0] = in_20; _29[31:0] = in_24; _30[31:0] = in_28; _31[31:0] = in_32; A1[4:0] = in_33
endmodule
