// Logisim project navigation.circ as structural Verilog: 3 circuits, main circuit navigation
module navigation (
  input  [1:0] dir,
  input  reset,
  output arrive,
  output hit
);

  wire clk, register_2_q, register_3_q, register_4_q, transfer_state_1_hit, transfer_state_1_ss0,
       transfer_state_1_ss1, transfer_state_1_ss2;

  Clock clock_1 (.out(clk));
  transfer_state transfer_state_1 (
    .S2(register_2_q), .S1(register_3_q), .S0(register_4_q), .A1(dir[1]), .A0(dir[0]),
    .SS2(transfer_state_1_ss2), .SS1(transfer_state_1_ss1), .SS0(transfer_state_1_ss0),
    .hit(transfer_state_1_hit));
  Register #(.width(1)) register_1 (.D(transfer_state_1_hit), .Q(hit), .clk(clk), .clr(reset));  // open: en
  // Probe on register_2_q
  // Probe on register_3_q
  Register #(.width(1)) register_2 (.D(transfer_state_1_ss2), .Q(register_2_q), .clk(clk), .clr(reset));  // open: en
  Register #(.width(1)) register_3 (.D(transfer_state_1_ss1), .Q(register_3_q), .clk(clk), .clr(reset));  // open: en
  Register #(.width(1)) register_4 (.D(transfer_state_1_ss0), .Q(register_4_q), .clk(clk), .clr(reset));  // open: en
  // Probe on register_4_q
  \output  output_1 (.S2(register_2_q), .S1(register_3_q), .S0(register_4_q), .arrive(arrive));
endmodule

module \output  (
  input  S2,
  input  S1,
  input  S0,
  output arrive
);


  assign arrive = S2;
endmodule

module transfer_state (
  input  S2,
  input  S1,
  input  S0,
  input  A1,
  input  A0,
  output SS2,
  output SS1,
  output SS0,
  output hit
);

  wire and_1_out, and_2_out, and_3_out, and_4_out, and_5_out, and_6_out, and_7_out, and_8_out, and_9_out,
       and_10_out, and_11_out, and_12_out, and_13_out, and_14_out, and_15_out, and_16_out, and_17_out,
       and_18_out, and_19_out, and_20_out, and_21_out, and_22_out, and_23_out, and_24_out, and_25_out,
       and_26_out, and_27_out, and_28_out, and_29_out, and_30_out, and_31_out, and_32_out, and_33_out,
       and_34_out, and_35_out, and_36_out, and_37_out, and_38_out, and_39_out, and_40_out, and_41_out,
       and_42_out, and_43_out, and_44_out, and_45_out, and_46_out, and_47_out, not_1_out, not_2_out,
       not_3_out, not_4_out, not_5_out, not_6_out, not_7_out, not_8_out, not_9_out, not_10_out, not_11_out,
       not_12_out, not_13_out, not_14_out, not_15_out, not_16_out, not_17_out, not_18_out, not_19_out,
       not_20_out, not_21_out, not_22_out, not_23_out, not_24_out, not_25_out, not_26_out, not_27_out,
       not_28_out, not_29_out, not_30_out, not_31_out, not_32_out, not_33_out, or_2_out, or_3_out, or_4_out,
       or_5_out, or_6_out, or_7_out, or_8_out, or_9_out, or_10_out;

  not not_1 (not_1_out, S0);
  not not_2 (not_2_out, A1);
  not not_3 (not_3_out, A1);
  not not_4 (not_4_out, A0);
  not not_5 (not_5_out, S1);
  not not_6 (not_6_out, A1);
  not not_7 (not_7_out, S2);
  not not_8 (not_8_out, S1);
  not not_9 (not_9_out, S2);
  not not_10 (not_10_out, S1);
  not not_11 (not_11_out, S0);
  not not_12 (not_12_out, S2);
  not not_13 (not_13_out, S1);
  not not_14 (not_14_out, S0);
  not not_15 (not_15_out, S2);
  not not_16 (not_16_out, S1);
  not not_17 (not_17_out, S2);
  not not_18 (not_18_out, S0);
  not not_19 (not_19_out, S0);
  not not_20 (not_20_out, A1);
  not not_21 (not_21_out, A0);
  not not_22 (not_22_out, A1);
  and and_1 (and_1_out, S1, not_1_out);
  and and_2 (and_2_out, not_2_out, A0);
  and and_3 (and_3_out, S1, S0);
  and and_4 (and_4_out, not_3_out, not_4_out);
  and and_5 (and_5_out, not_5_out, S0);
  not not_23 (not_23_out, A1);
  and and_6 (and_6_out, S0, not_6_out);
  not not_24 (not_24_out, S0);
  not not_25 (not_25_out, A1);
  not not_26 (not_26_out, A0);
  not not_27 (not_27_out, S0);
  not not_28 (not_28_out, A0);
  and and_7 (and_7_out, not_7_out, not_8_out);
  not not_29 (not_29_out, S0);
  not not_30 (not_30_out, A1);
  not not_31 (not_31_out, A0);
  and and_8 (and_8_out, not_9_out, not_10_out);
  and and_9 (and_9_out, not_11_out, A0);
  and and_10 (and_10_out, not_12_out, not_13_out);
  and and_11 (and_11_out, not_14_out, A1);
  and and_12 (and_12_out, not_15_out, not_16_out);
  and and_13 (and_13_out, A1, A0);
  and and_14 (and_14_out, not_17_out, not_18_out);
  and and_15 (and_15_out, A1, A0);
  and and_16 (and_16_out, S1, not_19_out);
  and and_17 (and_17_out, not_20_out, not_21_out);
  and and_18 (and_18_out, S1, S0);
  and and_19 (and_19_out, not_22_out, A0);
  not not_32 (not_32_out, A0);
  and and_20 (and_20_out, and_1_out, and_2_out);
  or or_1 (SS2, and_20_out, and_21_out);
  and and_21 (and_21_out, and_3_out, and_4_out);
  and and_22 (and_22_out, and_5_out, not_23_out);
  or or_2 (or_2_out, and_22_out, and_23_out);
  and and_23 (and_23_out, and_6_out, A0);
  and and_24 (and_24_out, S1, not_24_out);
  and and_25 (and_25_out, and_24_out, and_26_out);
  and and_26 (and_26_out, not_25_out, not_26_out);
  and and_27 (and_27_out, S1, not_27_out);
  and and_28 (and_28_out, and_27_out, and_29_out);
  and and_29 (and_29_out, A1, A0);
  and and_30 (and_30_out, S1, S0);
  and and_31 (and_31_out, and_30_out, and_32_out);
  and and_32 (and_32_out, A1, not_28_out);
  and and_33 (and_33_out, and_7_out, not_29_out);
  and and_34 (and_34_out, and_33_out, and_35_out);
  and and_35 (and_35_out, not_30_out, not_31_out);
  and and_36 (and_36_out, S0, A0);
  and and_37 (and_37_out, S1, A1);
  not not_33 (not_33_out, A0);
  and and_38 (and_38_out, and_8_out, and_9_out);
  or or_3 (or_3_out, and_38_out, and_39_out);
  and and_39 (and_39_out, and_10_out, and_11_out);
  and and_40 (and_40_out, and_12_out, and_13_out);
  or or_4 (or_4_out, and_40_out, and_41_out);
  and and_41 (and_41_out, and_14_out, and_15_out);
  and and_42 (and_42_out, and_16_out, and_17_out);
  or or_5 (or_5_out, and_42_out, and_43_out);
  and and_43 (and_43_out, and_18_out, and_19_out);
  and and_44 (and_44_out, S1, S0);
  and and_45 (and_45_out, and_44_out, and_46_out);
  and and_46 (and_46_out, A1, not_32_out);
  or or_6 (or_6_out, or_2_out, and_25_out);
  or or_7 (or_7_out, and_28_out, and_31_out);
  or or_8 (or_8_out, and_34_out, and_36_out);
  and and_47 (and_47_out, and_37_out, not_33_out);
  or or_9 (or_9_out, or_3_out, or_4_out);
  or or_10 (or_10_out, or_5_out, and_45_out);
  or or_11 (SS1, or_6_out, or_7_out);
  or or_12 (SS0, or_8_out, and_47_out);
  or or_13 (hit, or_9_out, or_10_out);
endmodule
