// Logisim project CPU-P3.circ as structural Verilog: 10 circuits, main circuit main
module main (
  input  Reset,
  output [31:0] Instr,
  output RegWrite,
  output [4:0] RegAddr,
  output [31:0] RegData,
  output MemWrite,
  output [4:0] MemAddr,
  output [31:0] MemData
);

  wire clk, Control_m3sel, zero;
  wire [1:0] Control_extop, Control_m1sel, Control_m2sel;
  wire [2:0] Control_aluop, Control_npcop;
  wire [4:0] IM_rd, IM_rs, IM_rt;
  wire [15:0] IM_imm;
  wire [25:0] IM_pc0_25;
  wire [31:0] ALU_c, EXT_ext, GRF_rd1, multiplexer_3_out, NPC_npc, NPC_pc_4, PC_q, ram_1_data;

  Clock clock_1 (.out(clk));
  Register #(.width(32)) PC (.D(NPC_npc), .Q(PC_q), .clk(clk), .clr(Reset));  // open: en
  NPC NPC (
    .zero(zero), .PC(PC_q), .imm(IM_imm), .NPC(NPC_npc), .NPCOp(Control_npcop), .instr_index(IM_pc0_25),
    .RA(GRF_rd1), .PC_4(NPC_pc_4));
  ROM #(.addrWidth(5), .dataWidth(32)) rom_1 (.addr(PC_q[6:2]), .data(Instr));  // open: sel
  IMSpritter IM (.Instr(Instr), .rs(IM_rs), .rt(IM_rt), .rd(IM_rd), .Imm(IM_imm), .PC0_25(IM_pc0_25));
  Control Control (
    .Instr(Instr), .NPCOp(Control_npcop), .RFWr(RegWrite), .EXTOp(Control_extop), .M3Sel(Control_m3sel),
    .ALUOp(Control_aluop), .DMWr(MemWrite), .M1Sel(Control_m1sel), .M2Sel(Control_m2sel));
  Multiplexer #(.select(2), .width(5), .disabled(0), .enable("false")) multiplexer_1 (
    .in0(IM_rt), .in1(IM_rd), .in2({5{1'b1}}), .out(RegAddr), .sel(Control_m1sel));  // open: in3
  Multiplexer #(.select(2), .width(32), .disabled(0), .enable("false")) multiplexer_2 (
    .in0({ALU_c[31:7], MemAddr, ALU_c[1:0]}), .in1(ram_1_data), .in2(NPC_pc_4), .out(RegData),
    .sel(Control_m2sel));  // open: in3
  GRF GRF (
    .RFWr(RegWrite), .clk(clk), .A1(IM_rs), .A2(IM_rt), .A3(RegAddr), .WD(RegData), .reset(Reset),
    .RD1(GRF_rd1), .RD2(MemData));
  EXT EXT (.Imm(IM_imm), .EXT(EXT_ext), .EXTOp(Control_extop));
  Multiplexer #(.width(32), .disabled(0), .enable("false")) multiplexer_3 (
    .in0(MemData), .in1(EXT_ext), .out(multiplexer_3_out), .sel(Control_m3sel));
  ALU ALU (
    .ALUOp(Control_aluop), .A(GRF_rd1), .B(multiplexer_3_out), .C({ALU_c[31:7], MemAddr, ALU_c[1:0]}),
    .zero(zero));
  RAM #(.addrWidth(5), .dataWidth(32), .bus("separate")) ram_1 (
    .addr(MemAddr), .din(MemData), .data(ram_1_data), .str(MemWrite), .clk(clk), .clr(Reset));  // open: sel, ld

  // Other names for the same wires on the sheet: DMWr = MemWrite
endmodule

module GRF (
  input  RFWr,
  input  clk,
  input  [4:0] A1,
  input  [4:0] A2,
  input  [4:0] A3,
  input  [31:0] WD,
  input  reset,
  output [31:0] RD1,
  output [31:0] RD2
);

  wire [31:0] _00, _000, _001, _01, _002, _02, _003, _03, _004, _04, _005, _05, _006, _06, _007, _07, _008,
       _08, _009, _09, _010, _10, _011, _11, _012, _12, _013, _13, _014, _14, _015, _15, _016, _16, _017,
       _17, _018, _18, _019, _19, _020, _20, _021, _21, _022, _22, _023, _23, _024, _24, _025, _25, _026,
       _26, _027, _27, _028, _28, _029, _29, _030, _30, _031, _31, and_1_out, and_2_out;

  Register #(.width(32)) u__00 (.D(_000), .en(RFWr), .Q(_00), .clk(clk), .clr(reset));
  Register #(.width(32)) u__01 (.D(_001), .en(RFWr), .Q(_01), .clk(clk), .clr(reset));
  Register #(.width(32)) u__02 (.D(_002), .en(RFWr), .Q(_02), .clk(clk), .clr(reset));
  Register #(.width(32)) u__03 (.D(_003), .en(RFWr), .Q(_03), .clk(clk), .clr(reset));
  Register #(.width(32)) u__04 (.D(_004), .en(RFWr), .Q(_04), .clk(clk), .clr(reset));
  Register #(.width(32)) u__05 (.D(_005), .en(RFWr), .Q(_05), .clk(clk), .clr(reset));
  Register #(.width(32)) u__06 (.D(_006), .en(RFWr), .Q(_06), .clk(clk), .clr(reset));
  Register #(.width(32)) u__07 (.D(_007), .en(RFWr), .Q(_07), .clk(clk), .clr(reset));
  Demultiplexer #(.select(5), .width(32), .tristate("true"), .disabled(0), .enable("false")) demultiplexer_1 (
    .out0(_000), .out1(_001), .out2(_002), .out3(_003), .out4(_004), .out5(_005), .out6(_006), .out7(_007),
    .out8(_008), .out9(_009), .out10(_010), .out11(_011), .out12(_012), .out13(_013), .out14(_014),
    .out15(_015), .out16(_016), .out17(_017), .out18(_018), .out19(_019), .out20(_020), .out21(_021),
    .out22(_022), .out23(_023), .out24(_024), .out25(_025), .out26(_026), .out27(_027), .out28(_028),
    .out29(_029), .out30(_030), .out31(_031), .in(WD), .sel(A3));
  Register #(.width(32)) u__08 (.D(_008), .en(RFWr), .Q(_08), .clk(clk), .clr(reset));
  Register #(.width(32)) u__09 (.D(_009), .en(RFWr), .Q(_09), .clk(clk), .clr(reset));
  Register #(.width(32)) u__10 (.D(_010), .en(RFWr), .Q(_10), .clk(clk), .clr(reset));
  Register #(.width(32)) u__11 (.D(_011), .en(RFWr), .Q(_11), .clk(clk), .clr(reset));
  Register #(.width(32)) u__12 (.D(_012), .en(RFWr), .Q(_12), .clk(clk), .clr(reset));
  Register #(.width(32)) u__13 (.D(_013), .en(RFWr), .Q(_13), .clk(clk), .clr(reset));
  Register #(.width(32)) u__14 (.D(_014), .en(RFWr), .Q(_14), .clk(clk), .clr(reset));
  Register #(.width(32)) u__15 (.D(_015), .en(RFWr), .Q(_15), .clk(clk), .clr(reset));
  Register #(.width(32)) u__16 (.D(_016), .en(RFWr), .Q(_16), .clk(clk), .clr(reset));
  Register #(.width(32)) u__17 (.D(_017), .en(RFWr), .Q(_17), .clk(clk), .clr(reset));
  Register #(.width(32)) u__18 (.D(_018), .en(RFWr), .Q(_18), .clk(clk), .clr(reset));
  Register #(.width(32)) u__19 (.D(_019), .en(RFWr), .Q(_19), .clk(clk), .clr(reset));
  Register #(.width(32)) u__20 (.D(_020), .en(RFWr), .Q(_20), .clk(clk), .clr(reset));
  Register #(.width(32)) u__21 (.D(_021), .en(RFWr), .Q(_21), .clk(clk), .clr(reset));
  Register #(.width(32)) u__22 (.D(_022), .en(RFWr), .Q(_22), .clk(clk), .clr(reset));
  Register #(.width(32)) u__23 (.D(_023), .en(RFWr), .Q(_23), .clk(clk), .clr(reset));
  Register #(.width(32)) u__24 (.D(_024), .en(RFWr), .Q(_24), .clk(clk), .clr(reset));
  Register #(.width(32)) u__25 (.D(_025), .en(RFWr), .Q(_25), .clk(clk), .clr(reset));
  Register #(.width(32)) u__26 (.D(_026), .en(RFWr), .Q(_26), .clk(clk), .clr(reset));
  Register #(.width(32)) u__27 (.D(_027), .en(RFWr), .Q(_27), .clk(clk), .clr(reset));
  Register #(.width(32)) u__28 (.D(_028), .en(RFWr), .Q(_28), .clk(clk), .clr(reset));
  Register #(.width(32)) u__29 (.D(_029), .en(RFWr), .Q(_29), .clk(clk), .clr(reset));
  Register #(.width(32)) u__30 (.D(_030), .en(RFWr), .Q(_30), .clk(clk), .clr(reset));
  Register #(.width(32)) u__31 (.D(_031), .en(RFWr), .Q(_31), .clk(clk), .clr(reset));
  // Probe on _00
  // Probe on _01
  // Probe on _02
  // Probe on _03
  // Probe on _04
  // Probe on _05
  // Probe on _06
  // Probe on _07
  // Probe on _08
  // Probe on _09
  // Probe on _10
  // Probe on _11
  // Probe on _12
  // Probe on _13
  // Probe on _14
  // Probe on _15
  assign and_1_out = {32{1'b0}} & _00;  // AND_Gate and_1, 32 bits wide
  // Probe on _16
  // Probe on _17
  // Probe on _18
  // Probe on _19
  // Probe on _20
  // Probe on _21
  // Probe on _22
  // Probe on _23
  // Probe on _24
  // Probe on _25
  // Probe on _26
  // Probe on _27
  // Probe on _28
  // Probe on _29
  // Probe on _30
  // Probe on _31
  Multiplexer #(.select(5), .width(32), .disabled(0), .enable("false")) multiplexer_1 (
    .in0(and_1_out), .in1(_01), .in2(_02), .in3(_03), .in4(_04), .in5(_05), .in6(_06), .in7(_07), .in8(_08),
    .in9(_09), .in10(_10), .in11(_11), .in12(_12), .in13(_13), .in14(_14), .in15(_15), .in16(_16),
    .in17(_17), .in18(_18), .in19(_19), .in20(_20), .in21(_21), .in22(_22), .in23(_23), .in24(_24),
    .in25(_25), .in26(_26), .in27(_27), .in28(_28), .in29(_29), .in30(_30), .in31(_31), .out(RD1), .sel(A1));
  assign and_2_out = {32{1'b0}} & _00;  // AND_Gate and_2, 32 bits wide
  Multiplexer #(.select(5), .width(32), .disabled(0), .enable("false")) multiplexer_2 (
    .in0(and_2_out), .in1(_01), .in2(_02), .in3(_03), .in4(_04), .in5(_05), .in6(_06), .in7(_07), .in8(_08),
    .in9(_09), .in10(_10), .in11(_11), .in12(_12), .in13(_13), .in14(_14), .in15(_15), .in16(_16),
    .in17(_17), .in18(_18), .in19(_19), .in20(_20), .in21(_21), .in22(_22), .in23(_23), .in24(_24),
    .in25(_25), .in26(_26), .in27(_27), .in28(_28), .in29(_29), .in30(_30), .in31(_31), .out(RD2), .sel(A2));
endmodule

module ALU (
  input  [2:0] ALUOp,
  input  [31:0] A,
  input  [31:0] B,
  output zero,
  output [31:0] C
);

  wire ALUF_c, ALUF_m1sel, comparator_1_lt;
  wire [31:0] adder_1_out, bit_extender_1_out, multiplexer_1_out, not_1_out, or_1_out;

  Multiplexer #(.width(32), .disabled(0), .enable("false")) multiplexer_1 (
    .in0(B), .in1(not_1_out), .out(multiplexer_1_out), .sel(ALUF_m1sel));
  assign not_1_out = ~B;  // NOT_Gate not_1, 32 bits wide
  ALUF ALUF (.ALUOp2(ALUOp[2]), .M1Sel(ALUF_m1sel), .ALUOp1(ALUOp[1]), .C(ALUF_c), .ALUOp0(ALUOp[0]));
  Adder #(.width(32)) adder_1 (.a(A), .b(multiplexer_1_out), .out(adder_1_out), .cin(ALUF_c));  // open: cout
  assign or_1_out = A | B;  // OR_Gate or_1, 32 bits wide
  Comparator #(.width(32), .mode("unsigned")) comparator_1 (.a(A), .b(B), .lt(comparator_1_lt));  // open: gt, eq
  assign bit_extender_1_out = {{31{1'b0}}, comparator_1_lt};  // Bit_Extender bit_extender_1
  Comparator #(.width(32), .mode("unsigned")) comparator_2 (
    .a(adder_1_out), .b({32{1'b0}}), .eq(zero));  // open: gt, lt
  Multiplexer #(.select(3), .width(32), .disabled(0), .enable("false")) multiplexer_2 (
    .in0(adder_1_out), .in1(adder_1_out), .in2(or_1_out), .in3(bit_extender_1_out), .out(C), .sel(ALUOp));  // open: in4, in5, in6, in7
endmodule

module ALUF (
  input  ALUOp2,
  input  ALUOp1,
  input  ALUOp0,
  output M1Sel,
  output C
);


  assign C = ALUOp0;
  assign M1Sel = ALUOp0;
endmodule

module EXT (
  input  [1:0] EXTOp,
  input  [15:0] Imm,
  output [31:0] EXT
);

  wire [31:0] bit_extender_1_out, bit_extender_2_out, shifter_1_out;

  assign bit_extender_1_out = {{16{Imm[15]}}, Imm};  // Bit_Extender bit_extender_1
  assign bit_extender_2_out = {{16{1'b0}}, Imm};  // Bit_Extender bit_extender_2
  // Probe on 5'b10000
  Shifter #(.width(32)) shifter_1 (.in(bit_extender_2_out), .\dist (5'b10000), .out(shifter_1_out));
  Multiplexer #(.select(2), .width(32), .disabled(0), .enable("false")) multiplexer_1 (
    .in0(bit_extender_1_out), .in1(bit_extender_2_out), .in2(shifter_1_out), .out(EXT), .sel(EXTOp));  // open: in3
endmodule

module IMSpritter (
  input  [31:0] Instr,
  output [4:0] rs,
  output [4:0] rt,
  output [4:0] rd,
  output [15:0] Imm,
  output [25:0] PC0_25
);


  assign Imm = Instr[15:0];
  assign PC0_25 = Instr[25:0];
  assign rd = Instr[15:11];
  assign rs = Instr[25:21];
  assign rt = Instr[20:16];
endmodule

module NPC (
  input  [2:0] NPCOp,
  input  zero,
  input  [31:0] PC,
  input  [15:0] imm,
  input  [25:0] instr_index,
  input  [31:0] RA,
  output [31:0] PC_4,
  output [31:0] NPC
);

  wire [31:0] adder_2_out, bit_extender_1_out, multiplexer_1_out, subtractor_1_out;

  Adder #(.width(32)) adder_1 (.a(32'h4), .b(PC), .out(PC_4));  // open: cin, cout
  assign bit_extender_1_out = {{14{imm[15]}}, {imm, 2'b00}};  // Bit_Extender bit_extender_1
  Adder #(.width(32)) adder_2 (.a(PC_4), .b(bit_extender_1_out), .out(adder_2_out));  // open: cin, cout
  Subtractor #(.width(32)) subtractor_1 (
    .a({PC[31:28], instr_index, 2'b00}), .b(32'h3000), .out(subtractor_1_out));  // open: bin, bout
  Multiplexer #(.width(32), .disabled(0), .enable("false")) multiplexer_1 (
    .in0(PC_4), .in1(adder_2_out), .out(multiplexer_1_out), .sel(zero));
  Multiplexer #(.select(3), .width(32), .disabled(0), .enable("false")) multiplexer_2 (
    .in0(PC_4), .in1(multiplexer_1_out), .in2(subtractor_1_out), .in3(RA), .out(NPC), .sel(NPCOp));  // open: in4, in5, in6, in7

  // Other names for the same wires on the sheet: PC28_31[3:0] = PC[31:28]
endmodule

module Control (
  input  [31:0] Instr,
  output [2:0] NPCOp,
  output [1:0] M1Sel,
  output [1:0] M2Sel,
  output RFWr,
  output [1:0] EXTOp,
  output M3Sel,
  output [2:0] ALUOp,
  output DMWr
);

  wire ControlAND_addu, ControlAND_beq, ControlAND_jal, ControlAND_jr, ControlAND_lui, ControlAND_lw,
       ControlAND_ori, ControlAND_sltu, ControlAND_subu, ControlAND_sw;

  Control_AND ControlAND (
    .op5(Instr[31]), .op4(Instr[30]), .op3(Instr[29]), .op2(Instr[28]), .op1(Instr[27]), .op0(Instr[26]),
    .fun5(Instr[5]), .fun4(Instr[4]), .fun3(Instr[3]), .fun2(Instr[2]), .fun1(Instr[1]), .fun0(Instr[0]),
    .ADDU(ControlAND_addu), .SUBU(ControlAND_subu), .ORI(ControlAND_ori), .LW(ControlAND_lw),
    .SW(ControlAND_sw), .BEQ(ControlAND_beq), .LUI(ControlAND_lui), .SLTU(ControlAND_sltu),
    .JAL(ControlAND_jal), .JR(ControlAND_jr));
  Control_OR ControlOR (
    .ADDU(ControlAND_addu), .SUBU(ControlAND_subu), .ORI(ControlAND_ori), .LW(ControlAND_lw),
    .SW(ControlAND_sw), .BEQ(ControlAND_beq), .LUI(ControlAND_lui), .NPCOp0(NPCOp[0]), .M1Sel0(M1Sel[0]),
    .M2Sel0(M2Sel[0]), .RFWr(RFWr), .EXTOp(EXTOp), .M3Sel(M3Sel), .ALUOp1(ALUOp[1]), .ALUOp0(ALUOp[0]),
    .DMWr(DMWr), .ALUOp2(ALUOp[2]), .SLTU(ControlAND_sltu), .JAL(ControlAND_jal), .JR(ControlAND_jr),
    .NPCOp1(NPCOp[1]), .NPCOp2(NPCOp[2]), .M1Sel1(M1Sel[1]), .M2Sel1(M2Sel[1]));
endmodule

module Control_AND (
  input  op5,
  input  op4,
  input  op3,
  input  op2,
  input  op1,
  input  op0,
  input  fun5,
  input  fun4,
  input  fun3,
  input  fun2,
  input  fun1,
  input  fun0,
  output ADDU,
  output SUBU,
  output ORI,
  output LW,
  output SLTU,
  output SW,
  output JR,
  output BEQ,
  output LUI,
  output JAL
);

  wire not_1_out, not_2_out, not_3_out, not_4_out, not_5_out, not_6_out, not_7_out, not_8_out, not_9_out,
       not_10_out, not_11_out, not_12_out, Rtype;

  not not_1 (not_1_out, fun5);
  not not_2 (not_2_out, fun4);
  not not_3 (not_3_out, fun3);
  not not_4 (not_4_out, fun2);
  not not_5 (not_5_out, fun1);
  not not_6 (not_6_out, fun0);
  and and_1 (ADDU, Rtype, fun0, not_5_out, not_4_out, not_3_out, not_2_out, fun5);
  and and_2 (SUBU, Rtype, fun0, fun1, not_4_out, not_3_out, not_2_out, fun5);
  and and_3 (SLTU, Rtype, fun0, fun1, not_4_out, fun3, not_2_out, fun5);
  and and_4 (JR, Rtype, not_6_out, not_5_out, not_4_out, fun3, not_2_out, not_1_out);
  not not_7 (not_7_out, op5);
  not not_8 (not_8_out, op4);
  not not_9 (not_9_out, op3);
  not not_10 (not_10_out, op2);
  not not_11 (not_11_out, op1);
  not not_12 (not_12_out, op0);
  and and_5 (Rtype, not_12_out, not_11_out, not_10_out, not_9_out, not_8_out, not_7_out);
  and and_6 (ORI, op0, not_11_out, op2, op3, not_8_out, not_7_out);
  and and_7 (LW, op0, op1, not_10_out, not_9_out, not_8_out, op5);
  and and_8 (SW, op0, op1, not_10_out, op3, not_8_out, op5);
  and and_9 (BEQ, not_12_out, not_11_out, op2, not_9_out, not_8_out, not_7_out);
  and and_10 (LUI, op0, op1, op2, op3, not_8_out, not_7_out);
  and and_11 (JAL, op0, op1, not_10_out, not_9_out, not_8_out, not_7_out);
endmodule

module Control_OR (
  input  JR,
  input  JAL,
  input  SLTU,
  input  ADDU,
  input  SUBU,
  input  ORI,
  input  LW,
  input  SW,
  input  BEQ,
  input  LUI,
  output NPCOp2,
  output NPCOp1,
  output NPCOp0,
  output M1Sel1,
  output M1Sel0,
  output M2Sel1,
  output M2Sel0,
  output RFWr,
  output M3Sel,
  output ALUOp2,
  output ALUOp1,
  output ALUOp0,
  output DMWr,
  output [1:0] EXTOp
);

  or or_1 (NPCOp1, JR, JAL);
  or or_2 (NPCOp0, JR, BEQ);
  or or_3 (M1Sel0, ADDU, SLTU, SUBU);
  or or_4 (RFWr, SLTU, ADDU, SUBU, JAL, LW, LUI, ORI);
  or or_5 (M3Sel, ORI, LW, SW, LUI);
  or or_6 (ALUOp1, SLTU, ORI);
  or or_7 (ALUOp0, SUBU, SLTU, BEQ);

  assign ALUOp2 = 1'b0;
  assign DMWr = SW;
  assign EXTOp = {LUI, ORI};
  assign M1Sel1 = JAL;
  assign M2Sel0 = LW;
  assign M2Sel1 = JAL;
  assign NPCOp2 = 1'b0;
endmodule
