// Logisim project 4bit_sort.circ as structural Verilog: 3 circuits, main circuit 4bit_sort
module _4bit_sort (
  input  [3:0] A,
  input  [3:0] B,
  input  [3:0] C,
  input  [3:0] D,
  output [3:0] _1,
  output [3:0] _2,
  output [3:0] _3,
  output [3:0] _4
);

  wire comparator_1_gt, comparator_2_gt, comparator_3_gt, comparator_4_gt, comparator_5_gt, comparator_6_gt;
  wire [3:0] n4bit_swap_1_out1, n4bit_swap_1_out2, n4bit_swap_2_out1, n4bit_swap_2_out2, n4bit_swap_3_out1,
       n4bit_swap_3_out2, n4bit_swap_4_out1, n4bit_swap_5_out1;

  Comparator #(.width(4), .mode("unsigned")) comparator_1 (.a(A), .b(B), .gt(comparator_1_gt));  // open: eq, lt
  _4bit_swap u_4bit_swap_1 (.in1(A), .in2(B), .S(comparator_1_gt), .Out1(n4bit_swap_1_out1), .Out2(n4bit_swap_1_out2));
  Comparator #(.width(4), .mode("unsigned")) comparator_2 (
    .a(n4bit_swap_1_out2), .b(C), .gt(comparator_2_gt));  // open: eq, lt
  _4bit_swap u_4bit_swap_2 (
    .in1(n4bit_swap_1_out2), .in2(C), .S(comparator_2_gt), .Out1(n4bit_swap_2_out1), .Out2(n4bit_swap_2_out2));
  Comparator #(.width(4), .mode("unsigned")) comparator_3 (
    .a(n4bit_swap_1_out1), .b(n4bit_swap_2_out1), .gt(comparator_3_gt));  // open: eq, lt
  Comparator #(.width(4), .mode("unsigned")) comparator_4 (
    .a(n4bit_swap_2_out2), .b(D), .gt(comparator_4_gt));  // open: eq, lt
  _4bit_swap u_4bit_swap_3 (
    .in1(n4bit_swap_1_out1), .in2(n4bit_swap_2_out1), .S(comparator_3_gt), .Out1(n4bit_swap_3_out1),
    .Out2(n4bit_swap_3_out2));
  _4bit_swap u_4bit_swap_4 (.in1(n4bit_swap_2_out2), .in2(D), .S(comparator_4_gt), .Out1(n4bit_swap_4_out1), .Out2(_4));
  Comparator #(.width(4), .mode("unsigned")) comparator_5 (
    .a(n4bit_swap_3_out2), .b(n4bit_swap_4_out1), .gt(comparator_5_gt));  // open: eq, lt
  _4bit_swap u_4bit_swap_5 (
    .in1(n4bit_swap_3_out2), .in2(n4bit_swap_4_out1), .S(comparator_5_gt), .Out1(n4bit_swap_5_out1), .Out2(_3));
  Comparator #(.width(4), .mode("unsigned")) comparator_6 (
    .a(n4bit_swap_3_out1), .b(n4bit_swap_5_out1), .gt(comparator_6_gt));  // open: eq, lt
  _4bit_swap u_4bit_swap_6 (
    .in1(n4bit_swap_3_out1), .in2(n4bit_swap_5_out1), .S(comparator_6_gt), .Out1(_1), .Out2(_2));
endmodule

module _1bit_swap (
  input  l1,
  input  l2,
  input  S,
  output O1,
  output O2
);

  wire and_1_out, and_2_out, and_3_out, and_4_out, not_1_out;

  not not_1 (not_1_out, S);
  and and_1 (and_1_out, l1, not_1_out);
  and and_2 (and_2_out, S, l2);
  and and_3 (and_3_out, l2, not_1_out);
  and and_4 (and_4_out, S, l1);
  or or_1 (O1, and_1_out, and_2_out);
  or or_2 (O2, and_3_out, and_4_out);
endmodule

module _4bit_swap (
  input  [3:0] in1,
  input  [3:0] in2,
  input  S,
  output [3:0] Out1,
  output [3:0] Out2
);

  _1bit_swap u_1bit_swap_1 (.l1(in1[0]), .l2(in2[0]), .S(S), .O1(Out1[0]), .O2(Out2[0]));
  _1bit_swap u_1bit_swap_2 (.l1(in1[1]), .l2(in2[1]), .S(S), .O1(Out1[1]), .O2(Out2[1]));
  _1bit_swap u_1bit_swap_3 (.l1(in1[2]), .l2(in2[2]), .S(S), .O1(Out1[2]), .O2(Out2[2]));
  _1bit_swap u_1bit_swap_4 (.l1(in1[3]), .l2(in2[3]), .S(S), .O1(Out1[3]), .O2(Out2[3]));
endmodule
