// Logisim project Fabonacci_challenge.circ as structural Verilog
module main (
  input  [31:0] in_1,
  output [31:0] Nth
);

  wire \begin , bit_extender_1_out, clk, comparator_2_eq, counter_1_q, enable, not_1_out, not_2_out;
  wire [31:0] a11, a12, a21, a22, mult_2_c11, mult_2_c12, mult_2_c21, mult_2_c22, mult_c11, mult_c12,
       mult_c21, mult_c22, multiplexer_1_out, mux_2_c11, mux_2_c12, mux_2_c21, mux_2_c22, mux_3_c11,
       mux_3_c12, mux_3_c21, mux_3_c22, mux_c11, mux_c12, mux_c21, mux_c22, r11, r12, r21, r22, register_1_q,
       shifter_1_out;

  Clock clock_1 (.out(clk));
  Counter #(.width(1), .max('h1), .ongoal("stay")) counter_1 (
    .Q(counter_1_q), .clk(clk), .clr(1'b0));  // open: load, D, count, carry
  Comparator #(.width(1), .mode("unsigned")) comparator_1 (.a(counter_1_q), .b(1'b1), .eq(\begin ));  // open: gt, lt
  matrix_mult mult (
    .a11(a11), .a12(a12), .a21(a21), .a22(a22), .b11(a11), .b12(a12), .b21(a21), .b22(a22), .c11(mult_c11),
    .c12(mult_c12), .c21(mult_c21), .c22(mult_c22));
  matrix_mux mux (
    .a11(32'h1), .a12({32{1'b0}}), .a21({32{1'b0}}), .a22(32'h1), .b11(a11), .select(bit_extender_1_out),
    .b12(a12), .b21(a21), .b22(a22), .c11(mux_c11), .c12(mux_c12), .c21(mux_c21), .c22(mux_c22));
  Shifter #(.width(32), .shift("lr")) shifter_1 (.in(register_1_q), .\dist (5'b00001), .out(shifter_1_out));
  // Probe on in_1
  Multiplexer #(.width(32), .disabled(0), .enable("false")) multiplexer_1 (
    .in0(in_1), .in1(shifter_1_out), .out(multiplexer_1_out), .sel(\begin ));
  matrix_mult mult_2 (
    .a11(r11), .a12(r12), .a21(r21), .a22(r22), .b11(mux_c11), .b12(mux_c12), .b21(mux_c21), .b22(mux_c22),
    .c11(mult_2_c11), .c12(mult_2_c12), .c21(mult_2_c21), .c22(mult_2_c22));
  Register #(.width(32)) register_1 (.D(multiplexer_1_out), .Q(register_1_q), .clk(clk), .clr(1'b0));  // open: en
  matrix_mux mux_2 (
    .a11(32'h1), .a12(32'h1), .a21(32'h1), .a22({32{1'b0}}), .b11(mult_c11), .select(\begin ),
    .b12(mult_c12), .b21(mult_c21), .b22(mult_c22), .c11(mux_2_c11), .c12(mux_2_c12), .c21(mux_2_c21),
    .c22(mux_2_c22));
  not not_1 (not_1_out, enable);
  matrix_mux mux_3 (
    .a11(32'h1), .a12({32{1'b0}}), .a21({32{1'b0}}), .a22(32'h1), .b11(mult_2_c11), .select(\begin ),
    .b12(mult_2_c12), .b21(mult_2_c21), .b22(mult_2_c22), .c11(mux_3_c11), .c12(mux_3_c12), .c21(mux_3_c21),
    .c22(mux_3_c22));
  not not_2 (not_2_out, enable);
  martix_register \reg  (
    .i11(mux_2_c11), .i12(mux_2_c12), .i21(mux_2_c21), .i22(mux_2_c22), .ena(not_1_out), .clk(clk),
    .reset(1'b0), .o11(a11), .o12(a12), .o21(a21), .o22(a22));
  martix_register reg_2 (
    .i11(mux_3_c11), .i12(mux_3_c12), .i21(mux_3_c21), .i22(mux_3_c22), .ena(not_2_out), .clk(clk),
    .reset(1'b0), .o11(r11), .o12(r12), .o21(r21), .o22(r22));
  Bit_Extender #(.in_width(32), .out_width(1)) bit_extender_1 (.in(register_1_q), .out(bit_extender_1_out));
  Multiplexer #(.disabled(0), .enable("false")) multiplexer_2 (
    .in0(1'b0), .in1(comparator_2_eq), .out(enable), .sel(\begin ));
  Comparator #(.width(32), .mode("unsigned")) comparator_2 (
    .a({32{1'b0}}), .b(register_1_q), .eq(comparator_2_eq));  // open: gt, lt
  // Probe on Nth
  Multiplexer #(.width(32), .disabled(0), .enable("false")) multiplexer_3 (
    .in0({32{1'b0}}), .in1(r12), .out(Nth), .sel(enable));
endmodule

module matrix_mult (
  input  [31:0] a11,
  input  [31:0] a12,
  input  [31:0] a21,
  input  [31:0] a22,
  input  [31:0] b11,
  input  [31:0] b12,
  input  [31:0] b21,
  input  [31:0] b22,
  output [31:0] c11,
  output [31:0] c12,
  output [31:0] c21,
  output [31:0] c22
);

  wire [31:0] multiplier_1_out, multiplier_2_out, multiplier_3_out, multiplier_4_out, multiplier_5_out,
       multiplier_6_out, multiplier_7_out, multiplier_8_out;

  Multiplier #(.width(32)) multiplier_1 (.a(a11), .b(b11), .out(multiplier_1_out));  // open: cin, cout
  Multiplier #(.width(32)) multiplier_2 (.a(a12), .b(b21), .out(multiplier_2_out));  // open: cin, cout
  Multiplier #(.width(32)) multiplier_3 (.a(a11), .b(b12), .out(multiplier_3_out));  // open: cin, cout
  Multiplier #(.width(32)) multiplier_4 (.a(a12), .b(b22), .out(multiplier_4_out));  // open: cin, cout
  Multiplier #(.width(32)) multiplier_5 (.a(a21), .b(b11), .out(multiplier_5_out));  // open: cin, cout
  Multiplier #(.width(32)) multiplier_6 (.a(a22), .b(b21), .out(multiplier_6_out));  // open: cin, cout
  Multiplier #(.width(32)) multiplier_7 (.a(a21), .b(b12), .out(multiplier_7_out));  // open: cin, cout
  Multiplier #(.width(32)) multiplier_8 (.a(a22), .b(b22), .out(multiplier_8_out));  // open: cin, cout
  Adder #(.width(32)) adder_1 (.a(multiplier_1_out), .b(multiplier_2_out), .out(c11));  // open: cin, cout
  Adder #(.width(32)) adder_2 (.a(multiplier_3_out), .b(multiplier_4_out), .out(c12));  // open: cin, cout
  Adder #(.width(32)) adder_3 (.a(multiplier_5_out), .b(multiplier_6_out), .out(c21));  // open: cin, cout
  Adder #(.width(32)) adder_4 (.a(multiplier_7_out), .b(multiplier_8_out), .out(c22));  // open: cin, cout
  // Probe on c11
  // Probe on c12
  // Probe on c21
  // Probe on c22
endmodule

module martix_register (
  input  [31:0] i11,
  input  [31:0] i12,
  input  [31:0] i21,
  input  [31:0] i22,
  input  ena,
  input  clk,
  input  reset,
  output [31:0] o11,
  output [31:0] o12,
  output [31:0] o21,
  output [31:0] o22
);

  Register #(.width(32)) register_1 (.D(i11), .en(ena), .Q(o11), .clk(clk), .clr(reset));
  Register #(.width(32)) register_2 (.D(i12), .en(ena), .Q(o12), .clk(clk), .clr(reset));
  Register #(.width(32)) register_3 (.D(i21), .en(ena), .Q(o21), .clk(clk), .clr(reset));
  Register #(.width(32)) register_4 (.D(i22), .en(ena), .Q(o22), .clk(clk), .clr(reset));
endmodule

module matrix_mux (
  input  [31:0] a11,
  input  [31:0] a12,
  input  [31:0] a21,
  input  [31:0] a22,
  input  [31:0] b11,
  input  select,
  input  [31:0] b12,
  input  [31:0] b21,
  input  [31:0] b22,
  output [31:0] c11,
  output [31:0] c12,
  output [31:0] c21,
  output [31:0] c22
);

  Multiplexer #(.width(32), .disabled(0)) multiplexer_1 (.in0(a11), .in1(b11), .out(c11), .sel(select));  // open: en
  Multiplexer #(.width(32), .disabled(0)) multiplexer_2 (.in0(a12), .in1(b12), .out(c12), .sel(select));  // open: en
  Multiplexer #(.width(32)) multiplexer_3 (.in0(a21), .in1(b21), .out(c21), .sel(select));  // open: en
  Multiplexer #(.width(32)) multiplexer_4 (.in0(a22), .in1(b22), .out(c22), .sel(select));  // open: en
endmodule
