// Logisim project Fibonacci.circ as structural Verilog: 4 circuits, main circuit main
module main (
  input  [2:0] in_1,
  output [3:0] out_2
);

  wire and_1_out, clock_1_out, comparator_1_eq, comparator_1_lt, or_1_out, or_2_out;
  wire [3:0] add_4_bit_1_out_3, compare_1_out_3, multiplexer_1_out, register_1_q, register_2_q;
  wire [7:0] bit_extender_1_out, counter_1_q;

  Clock clock_1 (.out(clock_1_out));
  Counter counter_1 (.D(bit_extender_1_out), .Q(counter_1_q), .clk(clock_1_out));  // open: load, count, carry, clr
  // Probe on bit_extender_1_out
  assign bit_extender_1_out = {{5{1'b0}}, in_1};  // Bit_Extender bit_extender_1
  // Probe on counter_1_q
  Comparator #(.mode("unsigned")) comparator_1 (
    .a(bit_extender_1_out), .b(counter_1_q), .eq(comparator_1_eq), .lt(comparator_1_lt));  // open: gt
  // Probe on add_4_bit_1_out_3
  Compare compare_1 (.in_1(add_4_bit_1_out_3), .in_2(4'b0001), .out_3(compare_1_out_3));
  or or_1 (or_1_out, in_1[0], in_1[1], in_1[2]);
  Register #(.width(4)) register_1 (.D(compare_1_out_3), .Q(register_1_q), .clk(clock_1_out));  // open: en, clr
  or or_2 (or_2_out, comparator_1_eq, comparator_1_lt);
  Add_4_bit add_4_bit_1 (.in_1(register_1_q), .in_2(register_2_q), .out_3(add_4_bit_1_out_3));
  Register #(.width(4)) register_2 (.D(register_1_q), .Q(register_2_q), .clk(clock_1_out));  // open: en, clr
  and and_1 (and_1_out, or_1_out, or_2_out);
  // Probe on multiplexer_1_out
  Multiplexer #(.width(4), .disabled(0), .enable("false")) multiplexer_1 (
    .in0(4'b0000), .in1(register_1_q), .out(multiplexer_1_out), .sel(and_1_out));
  Register #(.width(4)) register_3 (
    .D(multiplexer_1_out), .en(comparator_1_eq), .Q(out_2), .clk(clock_1_out));  // open: clr
endmodule

module Add_1_bit (
  input  A,
  input  B,
  input  CI,
  output CO,
  output SO
);

  wire and_1_out, and_2_out, and_3_out, and_4_out, and_5_out, and_6_out, and_7_out, and_8_out, and_9_out,
       and_10_out, and_11_out, not_1_out, not_2_out, not_3_out, not_4_out, not_5_out, not_6_out, or_1_out,
       or_3_out, or_4_out;

  and and_1 (and_1_out, B, CI);
  and and_2 (and_2_out, A, CI);
  not not_1 (not_1_out, A);
  not not_2 (not_2_out, B);
  not not_3 (not_3_out, A);
  not not_4 (not_4_out, B);
  or or_1 (or_1_out, and_1_out, and_2_out);
  and and_3 (and_3_out, A, B);
  and and_4 (and_4_out, not_1_out, not_2_out);
  and and_5 (and_5_out, not_3_out, B);
  not not_5 (not_5_out, CI);
  and and_6 (and_6_out, A, not_4_out);
  not not_6 (not_6_out, CI);
  and and_7 (and_7_out, A, B);
  or or_2 (CO, or_1_out, and_3_out);
  and and_8 (and_8_out, and_4_out, CI);
  and and_9 (and_9_out, and_5_out, not_5_out);
  and and_10 (and_10_out, and_6_out, not_6_out);
  and and_11 (and_11_out, and_7_out, CI);
  or or_3 (or_3_out, and_8_out, and_9_out);
  or or_4 (or_4_out, and_10_out, and_11_out);
  or or_5 (SO, or_3_out, or_4_out);
endmodule

module Add_4_bit (
  input  [3:0] in_1,
  input  [3:0] in_2,
  output [3:0] out_3
);

  wire add_1_bit_1_co, add_1_bit_2_co, add_1_bit_3_co;

  // Probe on in_1
  // Probe on in_2
  Add_1_bit add_1_bit_1 (.A(in_1[0]), .B(in_2[0]), .CI(1'b0), .CO(add_1_bit_1_co), .SO(out_3[0]));
  Add_1_bit add_1_bit_2 (.A(in_1[1]), .B(in_2[1]), .CI(add_1_bit_1_co), .CO(add_1_bit_2_co), .SO(out_3[1]));
  Add_1_bit add_1_bit_3 (.A(in_1[2]), .B(in_2[2]), .CI(add_1_bit_2_co), .CO(add_1_bit_3_co), .SO(out_3[2]));
  Add_1_bit add_1_bit_4 (.A(in_1[3]), .B(in_2[3]), .CI(add_1_bit_3_co), .SO(out_3[3]));  // open: CO
  // Probe on out_3
endmodule

module Compare (
  input  [3:0] in_1,
  input  [3:0] in_2,
  output [3:0] out_3
);

  wire comparator_1_gt;

  Comparator #(.width(4), .mode("unsigned")) comparator_1 (.a(in_1), .b(in_2), .gt(comparator_1_gt));  // open: eq, lt
  Multiplexer #(.width(4), .enable("false")) multiplexer_1 (.in0(in_2), .in1(in_1), .out(out_3), .sel(comparator_1_gt));
endmodule
