// Logisim project mod5.circ as structural Verilog: 2 circuits, main circuit mod5
module mod5 (
  input  in_1,
  output out_2,
  output out_3,
  output out_4,
  output out_5,
  output out_6
);

  wire clock_1_out, register_1_q;

  Clock clock_1 (.out(clock_1_out));
  Register #(.width(1)) register_1 (.D(in_1), .Q(register_1_q), .clk(clock_1_out));  // open: en, clr
  Output output_1 (
    .in1(register_1_q), .in0(in_1), .out_3(out_2), .out_4(out_3), .out_5(out_4), .out_6(out_5), .out_7(out_6));
endmodule

module Output (
  input  in1,
  input  in0,
  output out_3,
  output out_4,
  output out_5,
  output out_6,
  output out_7
);

  wire not_1_out, not_2_out;

  not not_1 (not_1_out, in1);
  not not_2 (not_2_out, in0);
  and and_1 (out_4, not_1_out, not_2_out);
  and and_2 (out_5, not_1_out, in0);
  and and_3 (out_6, in0, in1);
  and and_4 (out_7, in1, not_2_out);

  assign out_3 = 1'b0;
endmodule
