// Logisim project shifter.circ as structural Verilog: 2 circuits, main circuit main
module main (
  input  [15:0] in_1,
  input  [3:0] in_2,
  output [15:0] out_3
);

  wire [15:0] demultiplexer_1_out0, demultiplexer_1_out1, demultiplexer_2_out0, demultiplexer_2_out1,
       demultiplexer_3_out0, demultiplexer_3_out1, demultiplexer_4_out0, or_1_out, or_2_out, or_3_out;
  wire [15:8] demultiplexer_4_out1, demultiplexer_4_out1_2;

  Demultiplexer #(.width(16), .enable("false")) demultiplexer_1 (
    .out0(demultiplexer_1_out0), .out1(demultiplexer_1_out1), .in(in_1), .sel(in_2[0]));
  assign or_1_out = {demultiplexer_1_out1[14:0], 1'b0} | demultiplexer_1_out0;  // OR_Gate or_1, 16 bits wide
  Demultiplexer #(.width(16), .enable("false")) demultiplexer_2 (
    .out0(demultiplexer_2_out0), .out1(demultiplexer_2_out1), .in(or_1_out), .sel(in_2[1]));
  assign or_2_out = {demultiplexer_2_out1[13:0], 2'b00} | demultiplexer_2_out0;  // OR_Gate or_2, 16 bits wide
  Demultiplexer #(.width(16), .enable("false")) demultiplexer_3 (
    .out0(demultiplexer_3_out0), .out1(demultiplexer_3_out1), .in(or_2_out), .sel(in_2[2]));
  Demultiplexer #(.width(16), .enable("false")) demultiplexer_4 (
    .out0(demultiplexer_4_out0), .out1({demultiplexer_4_out1, demultiplexer_4_out1_2}), .in(or_3_out),
    .sel(in_2[3]));
  assign or_3_out = {demultiplexer_3_out1[11:0], 4'b0000} | demultiplexer_3_out0;  // OR_Gate or_3, 16 bits wide
  assign out_3 = {demultiplexer_4_out1_2, {8{1'b0}}} | demultiplexer_4_out0;  // OR_Gate or_4, 16 bits wide
endmodule

module try (
  input  [1:0] in_1,
  input  in_2,
  input  in_3,
  input  [1:0] in_4,
  input  [1:0] in_5,
  input  in_6,
  input  in_7,
  output [1:0] out_8,
  output [1:0] out_9,
  output [1:0] out_10
);

  Demultiplexer #(.width(2), .disabled(0)) demultiplexer_1 (
    .out0(out_8), .out1(out_9), .in(in_1), .sel(in_3), .en(in_2));
  Multiplexer #(.width(2)) multiplexer_1 (.in0(in_4), .in1(in_5), .out(out_10), .sel(in_6), .en(in_7));
endmodule
